# Fritzing sketch Final Design (saved by Fritzing 0.9.2b)
breadboards: 1

parts:
  Part1 = Arduino Uno (Rev3)
  Servo = Basic Servo
  ADXL345_Accelerometer = Triple Axis Accelerometer Breakout - ADXL345

nets:
  N1: Part1.D10_PWM/SS, Servo.pulse
  N2: Part1.A4/SDA, ADXL345_Accelerometer.SDA
  N3: Part1.A5/SCL, ADXL345_Accelerometer.SCL
  VCC: Part1.5V, Servo.vcc, ADXL345_Accelerometer.VCC
  GND: Part1.GND, Servo.gnd, ADXL345_Accelerometer.GND
